# Fritzing sketch sketch (saved by Fritzing 0.9.9b)
breadboards: 2

parts:
  U1 = LuaNode32 / ESP32 [part_number=ESP32S-PIN30]
  Součástka1 = MAX3232

nets:
  GND: U1.GND, Součástka1.GND
  VIN: U1.Vin, Součástka1.VCC
  N1: U1.RX2, Součástka1.RXD
  N2: U1.TX2, Součástka1.TXD

custom parts:
  LuaNode32 / ESP32: New Image for LuaNode32 DOIT ESP32 DEVKIT V1. Base parts from LuaNode32 / ESP32 ESP32 based LuaNode32 by G.Noorlander DOIT Esp32 DevKit v1 (30 pins long, 11 pins width) by Werner Rothschopf (modified by vanepp Dec 2018)
  MAX3232: A random MAX3232 Breakout Board from AliExpress (RS232-TTL-Converter)
